// Logisim project test7seg.circ as structural Verilog: 1 circuit, main circuit test7seg
module test7seg (
);

  wire dec7seg_1_a, dec7seg_1_b, dec7seg_1_c, dec7seg_1_d, dec7seg_1_e, dec7seg_1_f, dec7seg_1_g,
       vxdvdsxgv_sw1, vxdvdsxgv_sw2, vxdvdsxgv_sw3, vxdvdsxgv_sw4;

  DipSwitch #(.number(4)) vxdvdsxgv (
    .sw1(vxdvdsxgv_sw1), .sw2(vxdvdsxgv_sw2), .sw3(vxdvdsxgv_sw3), .sw4(vxdvdsxgv_sw4));
  dec7seg dec7seg_1 (
    .X3(vxdvdsxgv_sw1), .X2(vxdvdsxgv_sw2), .X1(vxdvdsxgv_sw3), .X0(vxdvdsxgv_sw4), .g(dec7seg_1_g),
    .f(dec7seg_1_f), .e(dec7seg_1_e), .d(dec7seg_1_d), .c(dec7seg_1_c), .b(dec7seg_1_b), .a(dec7seg_1_a));
  _7_Segment_Display Y (
    .g(dec7seg_1_g), .f(dec7seg_1_f), .a(dec7seg_1_a), .b(dec7seg_1_b), .e(dec7seg_1_e), .d(dec7seg_1_d),
    .c(dec7seg_1_c), .dp(1'b0));

  // Notes on the sheet:
  //   L3Info-PFO
  //   Nom-prénom
  //   Nom-prénom
endmodule
