// Logisim project test_CPT4Binary.circ as structural Verilog: 1 circuit, main circuit main
module main (
  input  load,
  input  inc,
  input  rst
);

  wire clk_out;
  wire [3:0] cpt4binary_1_q, DIN_sw4;

  Clock sysclk ();  // open: out
  Clock clk (.out(clk_out));
  DipSwitch #(.number(4)) DIN (.sw1(DIN_sw4[3]), .sw2(DIN_sw4[2]), .sw3(DIN_sw4[1]), .sw4(DIN_sw4[0]));
  CPT4Binary cpt4binary_1 (.D(DIN_sw4), .load(load), .inc(inc), .clk(clk_out), .rst(rst), .Q(cpt4binary_1_q));
  _7_Segment_Display L_7_Segment_Display_1 ();  // open: g, f, a, b, e, d, c, dp
  // BCD_to_7_Segment_decoder bcd_to_7_segment_decoder_1: pin names not known; wires that end beside it: DIN_sw4, load, inc, clk_out, rst, cpt4binary_1_q
  LED LED0 (.in(cpt4binary_1_q[0]));
  LED LED1 (.in(cpt4binary_1_q[1]));
  LED LED2 (.in(cpt4binary_1_q[2]));
  LED LED3 (.in(cpt4binary_1_q[3]));
endmodule
