// Logisim project DIGIT44_BCD.circ as structural Verilog: 2 circuits, main circuit DIGIT44_BCD
module DIGIT44_BCD (
  input  [7:0] P,
  input  inc,
  input  clk,
  input  rst,
  output [7:0] Q,
  output tick
);

  wire comparator_1_eq, comparator_1_gt, cpt4bcd_1_tick;
  wire [3:0] cpt4bcd_1_q, cpt4bcd_2_q;

  CPT4BCD cpt4bcd_1 (
    .D(4'b0000), .load(comparator_1_eq), .inc(inc), .clk(clk), .rst(rst), .Q(cpt4bcd_1_q),
    .Tick(cpt4bcd_1_tick));
  CPT4BCD cpt4bcd_2 (
    .D(4'b0000), .load(comparator_1_eq), .inc(cpt4bcd_1_tick), .clk(clk), .rst(rst), .Q(cpt4bcd_2_q),
    .Tick(tick));
  Comparator #(.mode("unsigned")) comparator_1 (
    .a({cpt4bcd_2_q, cpt4bcd_1_q}), .b(P), .gt(comparator_1_gt), .eq(comparator_1_eq));  // open: lt
  Multiplexer #(.width(8), .enable("false")) multiplexer_1 (
    .in0({cpt4bcd_2_q, cpt4bcd_1_q}), .in1({8{1'b0}}), .out(Q), .sel(comparator_1_gt));
endmodule

module test_DIGIT44_BCD (
  input  rst,
  input  [7:0] P,
  input  inc,
  output [7:0] Q,
  output tick
);

  wire clk_out, sysclk_out;

  Clock clk (.out(clk_out));
  Clock sysclk (.out(sysclk_out));
  DIGIT44_BCD digit44_bcd_1 (.P(P), .inc(inc), .clk(clk_out), .rst(rst), .Q(Q), .tick(tick));
  _7_Segment_Display u_7_segment_display_1 ();  // open: g, f, a, b, e, d, c, dp
  // BCD_to_7_Segment_decoder bcd_to_7_segment_decoder_1: pin names not known; wires that end beside it: sysclk_out, Q[7:4]
  // BCD_to_7_Segment_decoder bcd_to_7_segment_decoder_2: pin names not known; wires that end beside it: Q[3:0]
  _7_Segment_Display u_7_segment_display_2 ();  // open: g, f, a, b, e, d, c, dp
endmodule
