// Logisim project DIGIT44_BCD.circ as structural Verilog: 2 circuits, main circuit DIGIT44_BCD
module DIGIT44_BCD (
  input  [7:0] P,
  input  inc,
  input  clk,
  input  rst,
  output [7:0] Q,
  output tick
);

  wire and_1_out, comparator_1_eq, comparator_1_lt, cpt4bcd_1_tick;
  wire [3:0] cpt4bcd_1_q, cpt4bcd_2_q;

  CPT4BCD cpt4bcd_1 (.D(4'b0000), .load(tick), .inc(inc), .clk(clk), .rst(rst), .Q(cpt4bcd_1_q), .Tick(cpt4bcd_1_tick));
  and and_1 (and_1_out, cpt4bcd_1_tick, inc);
  CPT4BCD cpt4bcd_2 (.D(4'b0000), .load(tick), .inc(and_1_out), .clk(clk), .rst(rst), .Q(cpt4bcd_2_q));  // open: Tick
  Comparator #(.mode("unsigned")) comparator_1 (
    .a(P), .b({cpt4bcd_2_q, cpt4bcd_1_q}), .eq(comparator_1_eq), .lt(comparator_1_lt));  // open: gt
  and and_2 (tick, inc, comparator_1_eq);
  Multiplexer #(.width(8), .enable("false")) multiplexer_1 (
    .in0({cpt4bcd_2_q, cpt4bcd_1_q}), .in1({8{1'b0}}), .out(Q), .sel(comparator_1_lt));
endmodule

module test_DIGIT44_BCD (
  input  rst,
  input  [7:0] P,
  input  inc,
  output [7:0] Q,
  output tick
);

  wire clk_out;

  Clock clk (.out(clk_out));
  Clock sysclk ();  // open: out
  DIGIT44_BCD digit44_bcd_1 (.P(P), .inc(inc), .clk(clk_out), .rst(rst), .Q(Q), .tick(tick));
  // BCD_to_7_Segment_decoder bcd_to_7_segment_decoder_1: pin names not known; wires that end beside it: Q[7:4]
  _7_Segment_Display u_7_segment_display_1 ();  // open: g, f, a, b, e, d, c, dp
  // BCD_to_7_Segment_decoder bcd_to_7_segment_decoder_2: pin names not known; wires that end beside it: Q[3:0]
  _7_Segment_Display u_7_segment_display_2 ();  // open: g, f, a, b, e, d, c, dp
endmodule
