// Logisim project CPT4BCD.circ as structural Verilog: 1 circuit, main circuit CPT4BCD
module CPT4BCD (
  input  [3:0] D,
  input  load,
  input  inc,
  input  clk,
  input  rst,
  output [3:0] Q,
  output Tick
);
endmodule
