// Logisim project CPT4Binary.circ as structural Verilog: 1 circuit, main circuit CPT4Binary
module CPT4Binary (
  input  [3:0] D,
  input  load,
  input  inc,
  input  clk,
  input  rst,
  output [3:0] Q
);

  wire xor_1_out;
  wire [3:0] adder_1_out, multiplexer_1_out;

  Adder #(.width(4)) adder_1 (.a(Q), .b(4'b0001), .out(adder_1_out), .cin(1'b0));  // open: cout
  Multiplexer #(.width(4), .enable("false")) multiplexer_1 (
    .in0(adder_1_out), .in1(D), .out(multiplexer_1_out), .sel(load));
  xor xor_1 (xor_1_out, load, inc);
  Register #(.width(4)) register_1 (.D(multiplexer_1_out), .en(xor_1_out), .clk(clk), .Q(Q), .clr(rst));
endmodule
