// Logisim project TP3.circ as structural Verilog: 4 circuits, main circuit test_sreg8
module chenillard_fsm (
  input  in_1
);

  wire clock_1_out;
  wire [7:0] fsm_entity_1_p4;

  Clock clock_1 (.out(clock_1_out));
  // FSM_Entity #(.content("fsm chenillard @[ 50 , 50 , 850 , 650 ]\n{ out L [ 8 ] @[ 864 , 187 , 36 , 15 ]\n;\ncodeWidth = 4 ; reset = S0 ; state S0 = \"0000\" @[ 112 , 117 , 30 , 30 ]\n{\ncommands @[ 157 , 132 , 86 , 22 ]\n{\nL = \"00000001\" ;\n}\ntransitions {\nS0 -> S1 when default @[ 208 , 98 , 43 , 22 ]\n;\n}\n}\nstate S1 = \"0001\" @[ 300 , 119 , 30 , 30 ]\n{\ncommands @[ 345 , 134 , 86 , 22 ]\n{\nL = \"00000010\" ;\n}\ntransitions {\nS1 -> S2 when default @[ 380 , 92 , 43 , 22 ]\n;\n}\n}\nstate S2 = \"0010\" @[ 454 , 120 , 30 , 30 ]\n{\ncommands @[ 499 , 135 , 86 , 22 ]\n{\nL = \"00000100\" ;\n}\ntransitions {\nS2 -> S3 when default @[ 543 , 90 , 43 , 22 ]\n;\n}\n}\nstate S3 = \"0011\" @[ 611 , 121 , 30 , 30 ]\n{\ncommands @[ 656 , 136 , 86 , 22 ]\n{\nL = \"00001000\" ;\n}\ntransitions {\nS3 -> S4 when default @[ 702 , 93 , 43 , 22 ]\n;\n}\n}\nstate S4 = \"0100\" @[ 778 , 125 , 30 , 30 ]\n{\ncommands @[ 823 , 140 , 93 , 22 ]\n{\nL = \"000010000\" ;\n}\ntransitions {\nS4 -> S5 when default @[ 818 , 210 , 43 , 22 ]\n;\n}\n}\nstate S5 = \"0101\" @[ 783 , 253 , 30 , 30 ]\n{\ncommands @[ 828 , 268 , 86 , 22 ]\n{\nL = \"00100000\" ;\n}\ntransitions {\nS5 -> S6 when default @[ 813 , 322 , 43 , 22 ]\n;\n}\n}\nstate S6 = \"0110\" @[ 785 , 357 , 30 , 30 ]\n{\ncommands @[ 830 , 372 , 86 , 22 ]\n{\nL = \"01000000\" ;\n}\ntransitions {\nS6 -> S7 when default @[ 809 , 441 , 43 , 22 ]\n;\n}\n}\nstate S7 = \"0111\" @[ 790 , 484 , 30 , 30 ]\n{\ncommands @[ 835 , 499 , 86 , 22 ]\n{\nL = \"10000000\" ;\n}\ntransitions {\nS7 -> S8 when default @[ 707 , 537 , 43 , 22 ]\n;\n}\n}\nstate S8 = \"1000\" @[ 601 , 490 , 30 , 30 ]\n{\ncommands @[ 593 , 543 , 86 , 22 ]\n{\nL = \"01000000\" ;\n}\ntransitions {\nS8 -> S9 when default @[ 521 , 532 , 43 , 22 ]\n;\n}\n}\nstate S9 = \"1001\" @[ 430 , 492 , 30 , 30 ]\n{\ncommands @[ 416 , 546 , 86 , 22 ]\n{\nL = \"00100000\" ;\n}\ntransitions {\nS9 -> S10 when default @[ 368 , 532 , 43 , 22 ]\n;\n}\n}\nstate S10 = \"1010\" @[ 290 , 496 , 30 , 30 ]\n{\ncommands @[ 278 , 553 , 93 , 22 ]\n{\nL = \"000010000\" ;\n}\ntransitions {\nS10 -> S11 when default @[ 214 , 551 , 43 , 22 ]\n;\n}\n}\nstate S11 = \"1011\" @[ 128 , 497 , 30 , 30 ]\n{\ncommands @[ 173 , 512 , 86 , 22 ]\n{\nL = \"00001000\" ;\n}\ntransitions {\nS11 -> S12 when default @[ 106 , 456 , 43 , 22 ]\n;\n}\n}\nstate S12 = \"1100\" @[ 105 , 365 , 30 , 30 ]\n{\ncommands @[ 148 , 379 , 86 , 22 ]\n{\nL = \"00000100\" ;\n}\ntransitions {\nS12 -> S13 when default @[ 76 , 331 , 43 , 22 ]\n;\n}\n}\nstate S13 = \"1101\" @[ 92 , 240 , 30 , 30 ]\n{\ncommands @[ 135 , 255 , 86 , 22 ]\n{\nL = \"00000010\" ;\n}\ntransitions {\nS13 -> S0 when default @[ 92 , 186 , 43 , 22 ]\n;\n}\n}\n}")) fsm_entity_1: pin names not known; wires that end beside it: clock_1_out, in_1, 1'b1, fsm_entity_1_p4
  LED LED0 (.in(fsm_entity_1_p4[0]));
  LED LED1 (.in(fsm_entity_1_p4[1]));
  LED LED2 (.in(fsm_entity_1_p4[2]));
  LED LED3 (.in(fsm_entity_1_p4[3]));
  LED LED4 (.in(fsm_entity_1_p4[4]));
  LED LED5 (.in(fsm_entity_1_p4[5]));
  LED LED6 (.in(fsm_entity_1_p4[6]));
  LED LED7 (.in(fsm_entity_1_p4[7]));
endmodule

module chenillard_sreg (
  input  rst,
  input  [7:0] in_2
);

  wire and_1_out, and_2_out, clk_out, comparator_1_eq, comparator_2_eq, nor_1_out, not_1_out, or_1_out,
       or_2_out, register_1_q;
  wire [1:0] multiplexer_1_out, multiplexer_2_out;
  wire [7:0] sreg8_1_q;

  Register #(.width(1)) register_1 (.D(or_1_out), .en(1'b1), .clk(clk_out), .Q(register_1_q), .clr(rst));
  or or_1 (or_1_out, and_2_out, and_1_out);
  Clock sysclk ();  // open: out
  Multiplexer #(.width(2), .enable("false")) multiplexer_1 (
    .in0(2'b10), .in1(2'b11), .out(multiplexer_1_out), .sel(or_2_out));
  or or_2 (or_2_out, register_1_q, sreg8_1_q[0]);
  Multiplexer #(.width(2), .enable("false")) multiplexer_2 (
    .in0(multiplexer_1_out), .in1(2'b01), .out(multiplexer_2_out), .sel(nor_1_out));
  Comparator #(.width(2), .mode("unsigned")) comparator_1 (
    .a(multiplexer_1_out), .b(2'b10), .eq(comparator_1_eq));  // open: gt, lt
  Comparator #(.width(2), .mode("unsigned")) comparator_2 (
    .a(multiplexer_1_out), .b(2'b11), .eq(comparator_2_eq));  // open: gt, lt
  Clock clk (.out(clk_out));
  nor nor_1 (nor_1_out, sreg8_1_q[0], sreg8_1_q[1], sreg8_1_q[2], sreg8_1_q[3], sreg8_1_q[4], sreg8_1_q[5], sreg8_1_q[6], sreg8_1_q[7]);
  and and_1 (and_1_out, sreg8_1_q[1], comparator_1_eq);
  not not_1 (not_1_out, sreg8_1_q[6]);
  and and_2 (and_2_out, not_1_out, comparator_2_eq);
  sreg8 sreg8_1 (.clk(clk_out), .d(in_2), .rst(rst), .lin(1'b0), .C(multiplexer_2_out), .rin(1'b0), .Q(sreg8_1_q));
  LED LED0 (.in(sreg8_1_q[0]));
  LED LED1 (.in(sreg8_1_q[1]));
  LED LED2 (.in(sreg8_1_q[2]));
  LED LED3 (.in(sreg8_1_q[3]));
  LED LED4 (.in(sreg8_1_q[4]));
  LED LED5 (.in(sreg8_1_q[5]));
  LED LED6 (.in(sreg8_1_q[6]));
  LED LED7 (.in(sreg8_1_q[7]));
endmodule

module sreg8 (
  input  [7:0] d,
  input  [1:0] C,
  input  rin,
  input  lin,
  input  clk,
  input  rst,
  output [7:0] Q
);

  wire [7:0] multiplexer_1_out;

  Multiplexer #(.select(2), .width(8), .enable("false")) multiplexer_1 (
    .in0(Q), .in1(d), .in2({rin, Q[7:1]}), .in3({Q[6:0], lin}), .out(multiplexer_1_out), .sel(C));
  Register register_1 (.D(multiplexer_1_out), .en(1'b1), .clk(clk), .Q(Q), .clr(rst));
endmodule

module test_sreg8 (
  input  rst,
  input  [1:0] C,
  input  rin,
  input  lin,
  input  [7:0] in_5
);

  wire clk_out;
  wire [7:0] sreg8_1_q;

  Clock sysclk ();  // open: out
  Clock clk (.out(clk_out));
  sreg8 sreg8_1 (.clk(clk_out), .d(in_5), .rst(rst), .lin(lin), .C(C), .rin(rin), .Q(sreg8_1_q));
  LED LED0 (.in(sreg8_1_q[0]));
  LED LED1 (.in(sreg8_1_q[1]));
  LED LED2 (.in(sreg8_1_q[2]));
  LED LED3 (.in(sreg8_1_q[3]));
  LED LED4 (.in(sreg8_1_q[4]));
  LED LED5 (.in(sreg8_1_q[5]));
  LED LED6 (.in(sreg8_1_q[6]));
  LED LED7 (.in(sreg8_1_q[7]));
endmodule
