// Logisim project Multiplieur8x8.circ as structural Verilog: 1 circuit, main circuit Multiplieur8x8
module Multiplieur8x8 (
  input  clk,
  input  rst,
  input  [7:0] A,
  input  [7:0] B,
  input  REQ,
  output ACK,
  output [15:0] RES
);

  wire comparator_2_eq, I, uc_mul_1_p7, WE;
  wire [3:0] adder_1_out, i_q, multiplexer_3_out;
  wire [7:0] mB_q, multiplexer_1_out, shifter_1_out;
  wire [15:0] adder_2_out, mA_q, multiplexer_2_out, multiplexer_4_out, multiplexer_5_out, shifter_2_out;

  // FSM_Entity #(.content("fsm UC_MUL @[ 88 , 45 , 800 , 500 ]\n{ in REQ [ 1 ] @[ 88 , 161 , 32 , 15 ]\n;\nin I [ 1 ] @[ 88 , 295 , 9 , 15 ]\n;\nout ACK [ 1 ] @[ 858 , 143 , 30 , 15 ]\n;\nout Load [ 1 ] @[ 854 , 230 , 34 , 15 ]\n;\nout WE [ 1 ] @[ 863 , 292 , 25 , 15 ]\n;\ncodeWidth = 4 ; reset = IDLE ; state IDLE = \"0000\" @[ 232 , 146 , 30 , 30 ]\n{\ncommands @[ 181 , 117 , 58 , 54 ]\n{\nLoad = \"0\" ;\nACK = \"0\" ;\nWE = \"0\" ;\n}\ntransitions {\nIDLE -> S1 when REQ @[ 345 , 123 , 32 , 22 ]\n;\n}\n}\nstate S1 = \"0001\" @[ 455 , 80 , 30 , 30 ]\n{\ncommands @[ 439 , 132 , 58 , 54 ]\n{\nLoad = \"0\" ;\nACK = \"0\" ;\nWE = \"1\" ;\n}\ntransitions {\nS1 -> S2 when REQ @[ 567 , 103 , 32 , 22 ]\n;\n}\n}\nstate S3 = \"0011\" @[ 493 , 222 , 30 , 30 ]\n{\ncommands @[ 538 , 237 , 58 , 54 ]\n{\nLoad = \"0\" ;\nACK = \"1\" ;\nWE = \"0\" ;\n}\ntransitions {\nS3 -> IDLE when / REQ @[ 359 , 222 , 43 , 22 ]\n;\n}\n}\nstate S2 = \"0010\" @[ 671 , 103 , 30 , 30 ]\n{\ncommands @[ 716 , 118 , 58 , 54 ]\n{\nLoad = \"1\" ;\nACK = \"0\" ;\nWE = \"1\" ;\n}\ntransitions {\nS2 -> S3 when I @[ 625 , 203 , 9 , 22 ]\n;\n}\n}\n}")) uc_mul_1: pin names not known; wires that end beside it: clk, rst, 1'b1, REQ, I, ACK, uc_mul_1_p7, WE
  Shifter #(.shift("lr")) shifter_1 (.in(mB_q), .\dist (3'b001), .out(shifter_1_out));
  Shifter #(.width(16)) shifter_2 (.in(mA_q), .\dist (4'b0001), .out(shifter_2_out));
  Multiplexer #(.width(8), .enable("false")) multiplexer_1 (
    .in0(B), .in1(shifter_1_out), .out(multiplexer_1_out), .sel(uc_mul_1_p7));
  Multiplexer #(.width(16), .enable("false")) multiplexer_2 (
    .in0({{8{1'b0}}, A}), .in1(shifter_2_out), .out(multiplexer_2_out), .sel(uc_mul_1_p7));
  Adder #(.width(4)) adder_1 (.a(i_q), .b(4'b0001), .out(adder_1_out));  // open: cin, cout
  Multiplexer #(.width(4), .enable("false")) multiplexer_3 (
    .in0(4'b0000), .in1(adder_1_out), .out(multiplexer_3_out), .sel(uc_mul_1_p7));
  Register mB (.D(multiplexer_1_out), .en(WE), .clk(clk), .Q(mB_q), .clr(rst));
  Register #(.width(16)) mA (.D(multiplexer_2_out), .en(WE), .clk(clk), .Q(mA_q), .clr(rst));
  Register #(.width(4)) u_i (.D(multiplexer_3_out), .en(WE), .clk(clk), .Q(i_q), .clr(rst));
  Comparator #(.width(4), .mode("unsigned")) comparator_1 (.a(i_q), .b(4'b0111), .eq(I));  // open: gt, lt
  Multiplexer #(.width(16), .enable("false")) multiplexer_4 (
    .in0({16{1'b0}}), .in1(mA_q), .out(multiplexer_4_out), .sel(comparator_2_eq));
  Comparator #(.width(1), .mode("unsigned")) comparator_2 (
    .a(mB_q[0]), .b(1'b1), .eq(comparator_2_eq));  // open: gt, lt
  Adder #(.width(16)) adder_2 (.a(multiplexer_4_out), .b(RES), .out(adder_2_out));  // open: cin, cout
  Multiplexer #(.width(16), .enable("false")) multiplexer_5 (
    .in0({16{1'b0}}), .in1(adder_2_out), .out(multiplexer_5_out), .sel(uc_mul_1_p7));
  Register #(.width(16)) ACC (.D(multiplexer_5_out), .en(WE), .clk(clk), .Q(RES), .clr(rst));
endmodule
