// Logisim project Multiplieur8x8_pt2.circ as structural Verilog: 1 circuit, main circuit Multiplieur8x8
module Multiplieur8x8 (
  input  clk,
  input  rst,
  input  [7:0] AB,
  input  REQ,
  output ACK,
  output [15:0] RES
);

  wire comparator_2_eq, InI, Load, RWA, RWB, RWC;
  wire [3:0] adder_1_out, i_q, multiplexer_3_out;
  wire [7:0] mB_q, multiplexer_1_out, shifter_1_out;
  wire [15:0] adder_2_out, mA_q, multiplexer_2_out, multiplexer_4_out, multiplexer_5_out, shifter_2_out;

  // FSM_Entity #(.content("fsm UC_MUL @[ 88 , 45 , 800 , 500 ]\n{ in REQ [ 1 ] @[ 88 , 161 , 32 , 15 ]\n;\nin I [ 1 ] @[ 88 , 295 , 9 , 15 ]\n;\nout ACK [ 1 ] @[ 858 , 143 , 30 , 15 ]\n;\nout Load [ 1 ] @[ 854 , 230 , 34 , 15 ]\n;\nout RWA [ 1 ] @[ 855 , 292 , 33 , 15 ]\n;\nout RWB [ 1 ] @[ 854 , 346 , 34 , 15 ]\n;\nout RWC [ 1 ] @[ 853 , 408 , 35 , 15 ]\n;\ncodeWidth = 4 ; reset = S0 ; state S1 = \"0001\" @[ 281 , 81 , 30 , 30 ]\n{\ncommands @[ 330 , 127 , 57 , 22 ]\n{\nRWA = \"1\" ;\n}\ntransitions {\nS1 -> S2 when REQ @[ 416 , 82 , 32 , 22 ]\n;\n}\n}\nstate S3 = \"0011\" @[ 708 , 88 , 30 , 30 ]\n{\ncommands @[ 752 , 87 , 54 , 22 ]\n{\nACK = \"0\" ;\n}\ntransitions {\nS3 -> S4 when REQ @[ 690 , 165 , 32 , 22 ]\n;\n}\n}\nstate S2 = \"0010\" @[ 490 , 83 , 30 , 30 ]\n{\ncommands @[ 511 , 133 , 57 , 38 ]\n{\nACK = \"1\" ;\nRWA = \"0\" ;\n}\ntransitions {\nS2 -> S3 when / REQ @[ 629 , 83 , 43 , 22 ]\n;\n}\n}\nstate S4 = \"0100\" @[ 702 , 210 , 30 , 30 ]\n{\ncommands @[ 753 , 240 , 59 , 38 ]\n{\nRWB = \"1\" ;\nRWC = \"1\" ;\n}\ntransitions {\nS4 -> S5 when REQ @[ 605 , 202 , 32 , 22 ]\n;\n}\n}\nstate S5 = \"0101\" @[ 478 , 208 , 30 , 30 ]\n{\ncommands @[ 514 , 259 , 59 , 70 ]\n{\nLoad = \"1\" ;\nRWA = \"1\" ;\nRWB = \"1\" ;\nRWC = \"1\" ;\n}\ntransitions {\nS5 -> S6 when I @[ 399 , 207 , 9 , 22 ]\n;\n}\n}\nstate S6 = \"0110\" @[ 281 , 209 , 30 , 30 ]\n{\ncommands @[ 334 , 247 , 59 , 86 ]\n{\nLoad = \"0\" ;\nACK = \"1\" ;\nRWA = \"0\" ;\nRWB = \"0\" ;\nRWC = \"0\" ;\n}\ntransitions {\nS6 -> S7 when / REQ @[ 216 , 242 , 43 , 22 ]\n;\n}\n}\nstate S0 = \"0000\" @[ 138 , 84 , 30 , 30 ]\n{\ncommands @[ 183 , 99 , 30 , 20 ]\n{\n}\ntransitions {\nS0 -> S1 when REQ @[ 234 , 89 , 32 , 22 ]\n;\n}\n}\nstate S7 = \"0111\" @[ 136 , 202 , 30 , 30 ]\n{\ncommands @[ 132 , 256 , 54 , 22 ]\n{\nACK = \"0\" ;\n}\ntransitions {\nS7 -> S1 when REQ @[ 218 , 161 , 32 , 22 ]\n;\n}\n}\n}")) uc_mul_1: pin names not known; wires that end beside it: clk, rst, 1'b1, REQ, InI, ACK, Load, RWA, RWB, RWC
  Shifter #(.shift("lr")) shifter_1 (.in(mB_q), .\dist (3'b001), .out(shifter_1_out));
  Shifter #(.width(16)) shifter_2 (.in(mA_q), .\dist (4'b0001), .out(shifter_2_out));
  Multiplexer #(.width(8), .enable("false")) multiplexer_1 (
    .in0(AB), .in1(shifter_1_out), .out(multiplexer_1_out), .sel(Load));
  Multiplexer #(.width(16), .enable("false")) multiplexer_2 (
    .in0({{8{1'b0}}, AB}), .in1(shifter_2_out), .out(multiplexer_2_out), .sel(Load));
  Adder #(.width(4)) adder_1 (.a(i_q), .b(4'b0001), .out(adder_1_out));  // open: cin, cout
  Multiplexer #(.width(4), .enable("false")) multiplexer_3 (
    .in0(4'b0000), .in1(adder_1_out), .out(multiplexer_3_out), .sel(Load));
  Register mB (.D(multiplexer_1_out), .en(RWB), .clk(clk), .Q(mB_q), .clr(rst));
  Register #(.width(16)) mA (.D(multiplexer_2_out), .en(RWA), .clk(clk), .Q(mA_q), .clr(rst));
  Register #(.width(4)) i (.D(multiplexer_3_out), .en(RWC), .clk(clk), .Q(i_q), .clr(rst));
  Comparator #(.width(4), .mode("unsigned")) comparator_1 (.a(i_q), .b(4'b0111), .eq(InI));  // open: gt, lt
  Multiplexer #(.width(16), .enable("false")) multiplexer_4 (
    .in0({16{1'b0}}), .in1(mA_q), .out(multiplexer_4_out), .sel(comparator_2_eq));
  Comparator #(.width(1), .mode("unsigned")) comparator_2 (
    .a(mB_q[0]), .b(1'b1), .eq(comparator_2_eq));  // open: gt, lt
  Adder #(.width(16)) adder_2 (.a(multiplexer_4_out), .b(RES), .out(adder_2_out));  // open: cin, cout
  Multiplexer #(.width(16), .enable("false")) multiplexer_5 (
    .in0({16{1'b0}}), .in1(adder_2_out), .out(multiplexer_5_out), .sel(Load));
  Register #(.width(16)) ACC (.D(multiplexer_5_out), .en(RWC), .clk(clk), .Q(RES), .clr(rst));
endmodule
