// Logisim project CPT4BCD.circ as structural Verilog: 1 circuit, main circuit CPT4BCD
module CPT4BCD (
  input  [3:0] D,
  input  load,
  input  inc,
  input  clk,
  input  rst,
  output [3:0] Q,
  output Tick
);

  wire or_1_out;
  wire [3:0] adder_1_out, multiplexer_1_out, multiplexer_2_out;

  Adder #(.width(4)) adder_1 (.a(Q), .b(4'b0001), .out(adder_1_out), .cin(1'b0));  // open: cout
  Multiplexer #(.width(4), .enable("false")) multiplexer_1 (
    .in0(adder_1_out), .in1(4'b0000), .out(multiplexer_1_out), .sel(Tick));
  Comparator #(.width(4), .mode("unsigned")) comparator_1 (.a(adder_1_out), .b(4'b1001), .gt(Tick));  // open: eq, lt
  Register #(.width(4)) register_1 (.D(multiplexer_2_out), .en(or_1_out), .clk(clk), .Q(Q), .clr(rst));
  Multiplexer #(.width(4), .enable("false")) multiplexer_2 (
    .in0(multiplexer_1_out), .in1(D), .out(multiplexer_2_out), .sel(load));
  or or_1 (or_1_out, load, inc);
endmodule
