// Logisim project DIGIT44_BCD.circ as structural Verilog: 2 circuits, main circuit DIGIT44_BCD
module DIGIT44_BCD (
  input  [7:0] P,
  input  inc,
  input  clk,
  input  rst,
  output [7:0] Q,
  output tick
);

  wire comparator_1_lt, cpt4bcd_1_tick;
  wire [3:0] cpt4bcd_1_q, cpt4bcd_2_q;

  CPT4BCD cpt4bcd_1 (.inc(inc), .clk(clk), .rst(rst), .Q(cpt4bcd_1_q), .Tick(cpt4bcd_1_tick));  // open: D, load
  CPT4BCD cpt4bcd_2 (.inc(cpt4bcd_1_tick), .clk(clk), .rst(rst), .Q(cpt4bcd_2_q), .Tick(tick));  // open: D, load
  Comparator #(.mode("unsigned")) comparator_1 (
    .a(P), .b({cpt4bcd_2_q, cpt4bcd_1_q}), .lt(comparator_1_lt));  // open: gt, eq
  Multiplexer #(.width(8), .enable("false")) multiplexer_1 (
    .in0({cpt4bcd_2_q, cpt4bcd_1_q}), .in1({8{1'b0}}), .out(Q), .sel(comparator_1_lt));
endmodule

module test_DIGIT44_BCD (
  input  rst,
  input  [7:0] P,
  input  inc,
  output [7:0] Q,
  output tick
);

  wire clk_out, sysclk_out;

  Clock sysclk (.out(sysclk_out));
  Clock clk (.out(clk_out));
  // DIGIT44_BCD digit44_bcd_1: pin names not known; wires that end beside it: clk_out, rst, P, inc, Q, tick
endmodule
