// Logisim project BCD_WATCH.circ as structural Verilog: 1 circuit, main circuit Watch
module Watch (
  input  rst
);

  wire clk_out, MM_tick, SS_tick;
  wire [7:0] HH_q, MM_q, SS_q;

  Clock clk (.out(clk_out));
  DIGIT44_BCD SS (.P(8'h59), .inc(1'b1), .clk(clk_out), .rst(rst), .Q(SS_q), .tick(SS_tick));
  DIGIT44_BCD MM (.P(8'h59), .inc(SS_tick), .clk(clk_out), .rst(rst), .Q(MM_q), .tick(MM_tick));
  DIGIT44_BCD HH (.P(8'h23), .inc(MM_tick), .clk(clk_out), .rst(rst), .Q(HH_q));  // open: tick
  // BCD_to_7_Segment_decoder bcd_to_7_segment_decoder_1: pin names not known
  // _7_Segment_Display H1: pin names not known; wires that end beside it: HH_q[7:4], HH_q[3:0]
  _7_Segment_Display H0 ();  // open: g, f, a, b, e, d, c, dp
  // BCD_to_7_Segment_decoder bcd_to_7_segment_decoder_2: pin names not known
  // BCD_to_7_Segment_decoder bcd_to_7_segment_decoder_3: pin names not known
  // _7_Segment_Display M1: pin names not known; wires that end beside it: MM_q[7:4], MM_q[3:0]
  _7_Segment_Display M0 ();  // open: g, f, a, b, e, d, c, dp
  // BCD_to_7_Segment_decoder bcd_to_7_segment_decoder_4: pin names not known
  _7_Segment_Display S0 ();  // open: g, f, a, b, e, d, c, dp
  // _7_Segment_Display S1: pin names not known; wires that end beside it: SS_q[7:4], SS_q[3:0]
  // BCD_to_7_Segment_decoder bcd_to_7_segment_decoder_5: pin names not known
  // BCD_to_7_Segment_decoder bcd_to_7_segment_decoder_6: pin names not known

  // Notes on the sheet:
  //   TP2 montre numérique 
endmodule
