// Logisim project TP31.circ as structural Verilog: 4 circuits, main circuit chenillard_fsm
module chenillard_fsm (
  input  in_1
);

  wire clock_1_out;
  wire [7:0] undriven;

  Clock clock_1 (.out(clock_1_out));
  LED LED0 (.in(undriven[0]));
  LED LED1 (.in(undriven[1]));
  LED LED2 (.in(undriven[2]));
  LED LED3 (.in(undriven[3]));
  LED LED4 (.in(undriven[4]));
  LED LED5 (.in(undriven[5]));
  LED LED6 (.in(undriven[6]));
  LED LED7 (.in(undriven[7]));
endmodule

module chenillard_sreg (
  input  rst,
  input  [7:0] in_2
);

  wire and_1_out, and_2_out, clk_out, comparator_1_eq, comparator_2_eq, d_ff_1_q, not_1_out, or_1_out,
       xnor_1_out;
  wire [1:0] multiplexer_1_out, multiplexer_2_out;
  wire [7:0] sreg8_1_q;

  D_Flip_Flop d_ff_1 (.D(or_1_out), .clk(clk_out), .Q(d_ff_1_q), .reset(rst));  // open: Qn, preset
  Clock clk (.out(clk_out));
  Multiplexer #(.width(2), .enable("false")) multiplexer_1 (
    .in0(2'b10), .in1(2'b11), .out(multiplexer_1_out), .sel(d_ff_1_q));
  Comparator #(.width(2), .mode("unsigned")) comparator_1 (
    .a(multiplexer_1_out), .b(2'b10), .eq(comparator_1_eq));  // open: gt, lt
  Comparator #(.width(2), .mode("unsigned")) comparator_2 (
    .a(multiplexer_1_out), .b(2'b11), .eq(comparator_2_eq));  // open: gt, lt
  NotExactlyOne xnor_1 (
    .out(xnor_1_out), .in0(sreg8_1_q[7]), .in1(sreg8_1_q[6]), .in2(sreg8_1_q[5]), .in3(sreg8_1_q[4]),
    .in4(sreg8_1_q[3]), .in5(sreg8_1_q[2]), .in6(sreg8_1_q[1]), .in7(sreg8_1_q[0]));
  not not_1 (not_1_out, sreg8_1_q[6]);
  Multiplexer #(.width(2), .enable("false")) multiplexer_2 (
    .in0(multiplexer_1_out), .in1(2'b01), .out(multiplexer_2_out), .sel(xnor_1_out));
  and and_1 (and_1_out, sreg8_1_q[1], comparator_1_eq);
  and and_2 (and_2_out, not_1_out, comparator_2_eq);
  or or_1 (or_1_out, and_1_out, and_2_out);
  sreg8 sreg8_1 (.rin(1'b0), .clk(clk_out), .C(multiplexer_2_out), .d(in_2), .lin(1'b0), .rst(rst), .Q(sreg8_1_q));
  LED LED0 (.in(sreg8_1_q[0]));
  LED LED1 (.in(sreg8_1_q[1]));
  LED LED2 (.in(sreg8_1_q[2]));
  LED LED3 (.in(sreg8_1_q[3]));
  LED LED4 (.in(sreg8_1_q[4]));
  LED LED6 (.in(sreg8_1_q[6]));
  LED LED7 (.in(sreg8_1_q[7]));
  LED LED5 (.in(sreg8_1_q[5]));
endmodule

module sreg8 (
  input  clk,
  input  rst,
  input  [1:0] C,
  input  rin,
  input  lin,
  input  [7:0] d,
  output [7:0] Q
);

  wire [7:0] multiplexer_1_out;

  Multiplexer #(.select(2), .width(8), .enable("false")) multiplexer_1 (
    .in0(Q), .in1(d), .in2({rin, Q[7:1]}), .in3({Q[6:0], lin}), .out(multiplexer_1_out), .sel(C));
  Register register_1 (.D(multiplexer_1_out), .en(1'b1), .clk(clk), .Q(Q), .clr(rst));
endmodule

module test_sreg8 (
  input  rst,
  input  [1:0] C,
  input  rin,
  input  lin,
  input  [7:0] in_5
);

  wire clk_out;
  wire [7:0] sreg8_1_q;

  Clock clk (.out(clk_out));
  sreg8 sreg8_1 (.rin(rin), .clk(clk_out), .C(C), .d(in_5), .lin(lin), .rst(rst), .Q(sreg8_1_q));
  LED LED0 (.in(sreg8_1_q[0]));
  LED LED1 (.in(sreg8_1_q[1]));
  LED LED2 (.in(sreg8_1_q[2]));
  LED LED3 (.in(sreg8_1_q[3]));
  LED LED4 (.in(sreg8_1_q[4]));
  LED LED5 (.in(sreg8_1_q[5]));
  LED LED6 (.in(sreg8_1_q[6]));
  LED LED7 (.in(sreg8_1_q[7]));
endmodule
