// Logisim project TP32.circ as structural Verilog: 4 circuits, main circuit test_sreg8
module chenillard_fsm (
  input  in_1
);

  wire clock_1_out;
  wire [7:0] fsm_entity_1_p4;

  Clock clock_1 (.out(clock_1_out));
  // FSM_Entity #(.content("fsm chenillard @[ 50 , 50 , 850 , 650 ]\n{ out L [ 8 ] @[ 864 , 187 , 36 , 15 ]\n;\ncodeWidth = 4 ; reset = S0 ; state S0 = \"0000\" @[ 104 , 123 , 30 , 30 ]\n{\ncommands @[ 149 , 138 , 86 , 22 ]\n{\nL = \"10000000\" ;\n}\ntransitions {\nS0 -> S1 when default @[ 204 , 81 , 43 , 22 ]\n;\n}\n}\nstate S1 = \"0001\" @[ 314 , 120 , 30 , 30 ]\n{\ncommands @[ 359 , 135 , 86 , 22 ]\n{\nL = \"01000000\" ;\n}\ntransitions {\nS1 -> S2 when default @[ 406 , 87 , 43 , 22 ]\n;\n}\n}\nstate S2 = \"0010\" @[ 463 , 111 , 30 , 30 ]\n{\ncommands @[ 506 , 126 , 86 , 22 ]\n{\nL = \"00100000\" ;\n}\ntransitions {\nS2 -> S3 when default @[ 598 , 87 , 43 , 22 ]\n;\n}\n}\nstate S3 = \"0011\" @[ 672 , 113 , 30 , 30 ]\n{\ncommands @[ 715 , 128 , 86 , 22 ]\n{\nL = \"00010000\" ;\n}\ntransitions {\nS3 -> S4 when default @[ 777 , 215 , 43 , 22 ]\n;\n}\n}\nstate S4 = \"0100\" @[ 692 , 285 , 30 , 30 ]\n{\ncommands @[ 735 , 300 , 86 , 22 ]\n{\nL = \"00001000\" ;\n}\ntransitions {\nS4 -> S5 when default @[ 720 , 418 , 43 , 22 ]\n;\n}\n}\nstate S5 = \"0101\" @[ 570 , 421 , 30 , 30 ]\n{\ncommands @[ 615 , 436 , 86 , 22 ]\n{\nL = \"00000100\" ;\n}\ntransitions {\nS5 -> S6 when default @[ 479 , 464 , 43 , 22 ]\n;\n}\n}\nstate S6 = \"0110\" @[ 377 , 422 , 30 , 30 ]\n{\ncommands @[ 423 , 438 , 86 , 22 ]\n{\nL = \"00000010\" ;\n}\ntransitions {\nS6 -> S7 when default @[ 326 , 451 , 43 , 22 ]\n;\n}\n}\nstate S7 = \"0111\" @[ 325 , 362 , 30 , 30 ]\n{\ncommands @[ 370 , 377 , 86 , 22 ]\n{\nL = \"00000001\" ;\n}\ntransitions {\nS7 -> S8 when default @[ 356 , 308 , 43 , 22 ]\n;\n}\n}\nstate S8 = \"1000\" @[ 416 , 294 , 30 , 30 ]\n{\ncommands @[ 459 , 309 , 86 , 22 ]\n{\nL = \"00000010\" ;\n}\ntransitions {\nS8 -> S9 when default @[ 455 , 269 , 43 , 22 ]\n;\n}\n}\nstate S9 = \"1001\" @[ 498 , 249 , 30 , 30 ]\n{\ncommands @[ 541 , 264 , 86 , 22 ]\n{\nL = \"00000100\" ;\n}\ntransitions {\nS9 -> S10 when default @[ 543 , 225 , 43 , 22 ]\n;\n}\n}\nstate S10 = \"1010\" @[ 581 , 225 , 30 , 30 ]\n{\ncommands @[ 625 , 240 , 86 , 22 ]\n{\nL = \"00001000\" ;\n}\ntransitions {\nS10 -> S11 when default @[ 494 , 228 , 43 , 22 ]\n;\n}\n}\nstate S11 = \"1011\" @[ 368 , 212 , 30 , 30 ]\n{\ncommands @[ 411 , 227 , 86 , 22 ]\n{\nL = \"00010000\" ;\n}\ntransitions {\nS11 -> S12 when default @[ 299 , 202 , 43 , 22 ]\n;\n}\n}\nstate S12 = \"1100\" @[ 192 , 218 , 30 , 30 ]\n{\ncommands @[ 235 , 233 , 86 , 22 ]\n{\nL = \"00100000\" ;\n}\ntransitions {\nS12 -> S13 when default @[ 181 , 276 , 43 , 22 ]\n;\n}\n}\nstate S13 = \"1101\" @[ 143 , 314 , 30 , 30 ]\n{\ncommands @[ 186 , 329 , 86 , 22 ]\n{\nL = \"01000000\" ;\n}\ntransitions {\nS13 -> S0 when default @[ 90 , 245 , 43 , 22 ]\n;\n}\n}\n}")) fsm_entity_1: pin names not known; wires that end beside it: clock_1_out, in_1, 1'b1, fsm_entity_1_p4
  LED LED0 (.in(fsm_entity_1_p4[0]));
  LED LED1 (.in(fsm_entity_1_p4[1]));
  LED LED2 (.in(fsm_entity_1_p4[2]));
  LED LED3 (.in(fsm_entity_1_p4[3]));
  LED LED4 (.in(fsm_entity_1_p4[4]));
  LED LED5 (.in(fsm_entity_1_p4[5]));
  LED LED6 (.in(fsm_entity_1_p4[6]));
  LED LED7 (.in(fsm_entity_1_p4[7]));
endmodule

module chenillard_sreg (
  input  rst
);

  wire clk_out;
  wire [7:0] undriven;

  Clock sysclk ();  // open: out
  Clock clk (.out(clk_out));
  sreg8 sreg8_1 ();  // open: rst, rin, lin, clk, d, C, Q
  LED LED0 (.in(undriven[0]));
  LED LED1 (.in(undriven[1]));
  LED LED2 (.in(undriven[2]));
  LED LED3 (.in(undriven[3]));
  LED LED4 (.in(undriven[4]));
  LED LED5 (.in(undriven[5]));
  LED LED6 (.in(undriven[6]));
  LED LED7 (.in(undriven[7]));
endmodule

module sreg8 (
  input  clk,
  input  rst,
  input  [1:0] C,
  input  rin,
  input  lin,
  input  [7:0] d,
  output [7:0] Q
);
endmodule

module test_sreg8 (
  input  rst,
  input  [1:0] C,
  input  rin,
  input  lin,
  input  [7:0] in_5
);

  wire clk_out;
  wire [7:0] sreg8_1_q;

  Clock sysclk ();  // open: out
  Clock clk (.out(clk_out));
  sreg8 sreg8_1 (.rst(rst), .rin(rin), .lin(lin), .clk(clk_out), .d(in_5), .C(C), .Q(sreg8_1_q));
  LED LED0 (.in(sreg8_1_q[0]));
  LED LED1 (.in(sreg8_1_q[1]));
  LED LED2 (.in(sreg8_1_q[2]));
  LED LED3 (.in(sreg8_1_q[3]));
  LED LED4 (.in(sreg8_1_q[4]));
  LED LED5 (.in(sreg8_1_q[5]));
  LED LED6 (.in(sreg8_1_q[6]));
  LED LED7 (.in(sreg8_1_q[7]));
endmodule
