// Logisim project Multiplieur8x8.circ as structural Verilog: 1 circuit, main circuit Multiplieur8x8
module Multiplieur8x8 (
  input  clk,
  input  rst,
  input  [7:0] A,
  input  [7:0] B,
  input  REQ,
  output ACK,
  output [15:0] RES
);

  wire comparator_1_lt, not_1_out, or_1_out, uc_mul_1_p6;
  wire [3:0] adder_1_out, i_q, multiplexer_3_out;
  wire [7:0] mB_q, multiplexer_2_out, shifter_1_out;
  wire [15:0] adder_2_out, mA_q, multiplexer_1_out, multiplexer_4_out, shifter_2_out;

  // FSM_Entity #(.content("fsm UC_MUL @[ 88 , 45 , 800 , 500 ]\n{ in REQ [ 1 ] @[ 88 , 161 , 32 , 15 ]\n;\nout ACK [ 1 ] @[ 858 , 143 , 30 , 15 ]\n;\nout O1 [ 1 ] @[ 866 , 224 , 22 , 15 ]\n;\ncodeWidth = 4 ; reset = IDLE ; state IDLE = \"0000\" @[ 268 , 155 , 30 , 30 ]\n{\ncommands @[ 311 , 170 , 46 , 22 ]\n{\nO1 = \"0\" ;\n}\ntransitions {\nIDLE -> S1 when REQ @[ 357 , 99 , 32 , 22 ]\n;\n}\n}\nstate S1 = \"0001\" @[ 463 , 133 , 30 , 30 ]\n{\ncommands @[ 514 , 105 , 54 , 54 ]\n{\nO1 = \"1\" ;\nACK = \"1\" ;\n}\ntransitions {\nS1 -> S2 when / REQ @[ 509 , 232 , 43 , 22 ]\n;\n}\n}\nstate S2 = \"0010\" @[ 427 , 289 , 30 , 30 ]\n{\ncommands @[ 483 , 300 , 54 , 22 ]\n{\nACK = \"0\" ;\n}\ntransitions {\nS2 -> IDLE when default @[ 271 , 290 , 43 , 22 ]\n;\n}\n}\n}")) uc_mul_1: pin names not known; wires that end beside it: clk, rst, 1'b1, REQ, ACK, uc_mul_1_p6
  Multiplexer #(.width(16), .enable("false")) multiplexer_1 (
    .in0({{8{1'b0}}, A}), .in1(shifter_2_out), .out(multiplexer_1_out), .sel(uc_mul_1_p6));
  Adder #(.width(4)) adder_1 (.a(i_q), .b(4'b0001), .out(adder_1_out));  // open: cin, cout
  Multiplexer #(.width(8), .enable("false")) multiplexer_2 (
    .in0(B), .in1(shifter_1_out), .out(multiplexer_2_out), .sel(uc_mul_1_p6));
  Register mB (.D(multiplexer_2_out), .en(comparator_1_lt), .clk(clk), .Q(mB_q), .clr(rst));
  Register #(.width(16)) mA (.D(multiplexer_1_out), .en(comparator_1_lt), .clk(clk), .Q(mA_q), .clr(rst));
  Register #(.width(4)) i (.D(multiplexer_3_out), .en(uc_mul_1_p6), .clk(clk), .Q(i_q), .clr(rst));
  Multiplexer #(.width(4), .enable("false")) multiplexer_3 (
    .in0(4'b0000), .in1(adder_1_out), .out(multiplexer_3_out), .sel(comparator_1_lt));
  Shifter #(.shift("lr")) shifter_1 (.in(mB_q), .\dist (3'b001), .out(shifter_1_out));
  Comparator #(.width(4), .mode("unsigned")) comparator_1 (.a(i_q), .b(4'b1000), .lt(comparator_1_lt));  // open: gt, eq
  Shifter #(.width(16)) shifter_2 (.in(mA_q), .\dist (4'b0001), .out(shifter_2_out));
  Adder #(.width(16)) adder_2 (.a(RES), .b(mA_q), .out(adder_2_out));  // open: cin, cout
  Multiplexer #(.width(16), .enable("false")) multiplexer_4 (
    .in0(adder_2_out), .in1({16{1'b0}}), .out(multiplexer_4_out), .sel(not_1_out));
  not not_1 (not_1_out, uc_mul_1_p6);
  Register #(.width(16)) ACC (.D(multiplexer_4_out), .en(or_1_out), .clk(clk), .Q(RES), .clr(rst));
  or or_1 (or_1_out, mB_q[0], not_1_out);
endmodule
